// Logisim project isatrabalho.circ as structural Verilog: 3 circuits, main circuit main
module main (
);

  wire button_1_out, clk, mux_ula, ula_1_out_5, wbreg;
  wire [2:0] opcodeula, undriven;
  wire [3:0] opcode;
  wire [13:0] rom_1_data;
  wire [17:0] adder_1_out, imm, multiplexer_1_out, PC_q, registradores_1_saidard, registradores_1_saidars1,
       registradores_1_saidars2, ula_1_out_6;

  Clock clock_1 (.out(clk));
  Register #(.width(18)) PC (.D(adder_1_out), .en(1'b1), .clk(clk), .Q(PC_q), .clr(button_1_out));
  Button button_1 (.out(button_1_out));
  // Probe on adder_1_out
  Adder #(.width(18)) adder_1 (.a(PC_q), .b(18'h1), .out(adder_1_out));  // open: cin, cout
  ROM #(.addrWidth(18), .dataWidth(18)) rom_1 (.addr(PC_q), .data({opcode, rom_1_data}));
  // Probe on {opcode, rom_1_data}
  assign imm = {{10{rom_1_data[7]}}, rom_1_data[7:0]};  // Bit_Extender bit_extender_1
  registradores registradores_1 (
    .dado(ula_1_out_6), .rs1(undriven), .rs2(rom_1_data[13:11]), .w(wbreg), .clk(clk),
    .saidars1(registradores_1_saidars1), .saidars2(registradores_1_saidars2),
    .saidard(registradores_1_saidard));  // open: rd
  // Probe on registradores_1_saidars1
  // Probe on registradores_1_saidars2
  Multiplexer #(.width(18)) multiplexer_1 (
    .in0(registradores_1_saidard), .in1(imm), .out(multiplexer_1_out), .sel(mux_ula));
  // Probe on multiplexer_1_out
  ULA ula_1 (
    .rs1(registradores_1_saidars1), .rs2(registradores_1_saidars2), .rd(multiplexer_1_out),
    .opcodeula(opcodeula), .out_5(ula_1_out_5), .out_6(ula_1_out_6));
  LED led_1 (.in(ula_1_out_5));
  // Probe on ula_1_out_6
endmodule

module registradores (
  input  [17:0] dado,
  input  [2:0] rs1,
  input  [2:0] rs2,
  input  [2:0] rd,
  input  w,
  input  clk,
  output [17:0] saidars1,
  output [17:0] saidars2,
  output [17:0] saidard
);

  wire demultiplexer_1_out1, demultiplexer_1_out2, demultiplexer_1_out3, demultiplexer_1_out4,
       demultiplexer_1_out5, demultiplexer_1_out6, demultiplexer_1_out7;
  wire [17:0] multiplexer_1_out, multiplexer_2_out, multiplexer_3_out, multiplexer_4_out, multiplexer_5_out,
       multiplexer_6_out, multiplexer_7_out, vr1, vr2, vr3, vr4, vr5, vr6, vr7;

  Demultiplexer #(.select(3)) demultiplexer_1 (
    .out1(demultiplexer_1_out1), .out2(demultiplexer_1_out2), .out3(demultiplexer_1_out3),
    .out4(demultiplexer_1_out4), .out5(demultiplexer_1_out5), .out6(demultiplexer_1_out6),
    .out7(demultiplexer_1_out7), .in(w), .sel(rd));  // open: out0
  Multiplexer #(.width(18)) multiplexer_1 (.in0(vr1), .in1(dado), .out(multiplexer_1_out), .sel(demultiplexer_1_out1));
  Multiplexer #(.width(18)) multiplexer_2 (.in0(vr2), .in1(dado), .out(multiplexer_2_out), .sel(demultiplexer_1_out2));
  Multiplexer #(.width(18)) multiplexer_3 (.in0(vr3), .in1(dado), .out(multiplexer_3_out), .sel(demultiplexer_1_out3));
  Multiplexer #(.width(18)) multiplexer_4 (.in0(vr4), .in1(dado), .out(multiplexer_4_out), .sel(demultiplexer_1_out4));
  Multiplexer #(.width(18)) multiplexer_5 (.in0(vr5), .in1(dado), .out(multiplexer_5_out), .sel(demultiplexer_1_out5));
  Multiplexer #(.width(18)) multiplexer_6 (.in0(vr6), .in1(dado), .out(multiplexer_6_out), .sel(demultiplexer_1_out6));
  Multiplexer #(.width(18)) multiplexer_7 (.in0(vr7), .in1(dado), .out(multiplexer_7_out), .sel(demultiplexer_1_out7));
  Register #(.width(18)) r1 (.D(multiplexer_1_out), .clk(clk), .Q(vr1));  // open: en, clr
  Register #(.width(18)) r2 (.D(multiplexer_2_out), .clk(clk), .Q(vr2));  // open: en, clr
  Register #(.width(18)) r3 (.D(multiplexer_3_out), .clk(clk), .Q(vr3));  // open: en, clr
  Register #(.width(18)) r4 (.D(multiplexer_4_out), .clk(clk), .Q(vr4));  // open: en, clr
  Register #(.width(18)) r5 (.D(multiplexer_5_out), .clk(clk), .Q(vr5));  // open: en, clr
  Register #(.width(18)) r6 (.D(multiplexer_6_out), .clk(clk), .Q(vr6));  // open: en, clr
  Register #(.width(18)) r7 (.D(multiplexer_7_out), .clk(clk), .Q(vr7));  // open: en, clr
  Multiplexer #(.select(3), .width(18)) multiplexer_8 (
    .in0({18{1'b0}}), .in1(vr1), .in2(vr2), .in3(vr3), .in4(vr4), .in5(vr5), .in6(vr6), .in7(vr7),
    .out(saidars1), .sel(rs1));
  Multiplexer #(.select(3), .width(18)) multiplexer_9 (
    .in0({18{1'b0}}), .in1(vr1), .in2(vr2), .in3(vr3), .in4(vr4), .in5(vr5), .in6(vr6), .in7(vr7),
    .out(saidars2), .sel(rs2));
  Multiplexer #(.select(3), .width(18)) multiplexer_10 (
    .in0({18{1'b0}}), .in1(vr1), .in2(vr2), .in3(vr3), .in4(vr4), .in5(vr5), .in6(vr6), .in7(vr7),
    .out(saidard), .sel(rd));

  // Notes on the sheet:
  //   r0
endmodule

module ULA (
  input  [17:0] rs1,
  input  [17:0] rs2,
  input  [17:0] rd,
  input  [2:0] opcodeula,
  output out_5,
  output [17:0] out_6
);

  wire [4:0] bit_extender_1_out, bit_extender_2_out;
  wire [17:0] add, E, FMA, multiplier_1_out, OU, SHIFTLEFT, SHIFTRIGHT, sub;

  Adder #(.width(18)) adder_1 (.a(rs1), .b(rs2), .out(add));  // open: cin, cout
  assign E = rs1 & rs2;  // AND_Gate and_1, 18 bits wide
  assign OU = rs1 | rs2;  // OR_Gate or_1, 18 bits wide
  Multiplier #(.width(18)) multiplier_1 (.a(rs1), .b(rs2), .out(multiplier_1_out));  // open: cin, cout
  Bit_Extender #(.in_width(18), .out_width(5)) bit_extender_1 (.in(rs2), .out(bit_extender_1_out));
  Shifter #(.width(18)) shifter_1 (.in(rs1), .\dist (bit_extender_2_out), .out(SHIFTLEFT));
  Bit_Extender #(.in_width(18), .out_width(5)) bit_extender_2 (.in(rs2), .out(bit_extender_2_out));
  Subtractor #(.width(18)) subtractor_1 (.a(rs1), .b(rs2), .out(sub));  // open: bin, bout
  Adder #(.width(18)) adder_2 (.a(multiplier_1_out), .b(rd), .out(FMA));  // open: cin, cout
  Shifter #(.shift("ar"), .width(18)) shifter_2 (.in(rs1), .\dist (bit_extender_1_out), .out(SHIFTRIGHT));
  Multiplexer #(.select(3), .width(18)) multiplexer_1 (
    .in0(add), .in1(E), .in2(OU), .in3(FMA), .in4(SHIFTRIGHT), .in5(SHIFTLEFT), .in6(add), .in7(sub),
    .out(out_6), .sel(opcodeula));
  Comparator #(.width(18)) comparator_1 (.a({18{1'b0}}), .b(out_6), .eq(out_5));  // open: gt, lt

  // Other names for the same wires on the sheet: nop[17:0] = add
endmodule
